# Fritzing sketch data-producer-2-arduino (saved by Fritzing 0.9.3b)

parts:
  Part1 = Arduino Mega 2560 (Rev3)
  GLCD_128x1 = 128 x 64 Graphic LCD  # not connected
  DHT1 = DHT11 Humitidy and Temperature Sensor

nets:
  3V3: Part1.3V3, DHT1.VDD
  GND: Part1.GND, DHT1.GND
  N1: Part1.D22, DHT1.DATA

custom parts:
  DHT11 Humitidy and Temperature Sensor: DHT11 Humidity and Temperature Sensor
